// Logisim project 7-segment display decoder.circ as structural Verilog: 8 circuits, main circuit Final Result
module _7_Segment_Display_decoder (
  input  i0,
  input  i1,
  input  i2,
  input  i3,
  output o1,
  output o2,
  output o3,
  output o4,
  output o5,
  output o6,
  output o7
);

  wire and_1_out, and_2_out, and_3_out, and_4_out, and_5_out, and_6_out, and_7_out, and_8_out, and_9_out,
       and_10_out, and_11_out, and_12_out, and_13_out, and_14_out, and_15_out, and_16_out, and_17_out,
       and_18_out, and_19_out, and_20_out, and_21_out, and_22_out, and_23_out, and_24_out, and_25_out,
       and_26_out, and_27_out, and_28_out, and_29_out, and_30_out, and_31_out, and_32_out, and_33_out,
       and_34_out, and_35_out, not_1_out, not_2_out, not_3_out, not_4_out, not_5_out, not_6_out, not_7_out,
       not_8_out, not_9_out, not_10_out, not_11_out, not_12_out, not_13_out, not_14_out, not_15_out,
       not_16_out, not_17_out, not_18_out, not_19_out, not_20_out, not_21_out, not_22_out, not_23_out,
       not_24_out, not_25_out, not_26_out, not_27_out, not_28_out, not_29_out, not_30_out, not_31_out,
       not_32_out, not_33_out, not_34_out, not_35_out, not_36_out, not_37_out, not_38_out, not_39_out,
       not_40_out, not_41_out, not_42_out, not_43_out, not_44_out;

  not not_1 (not_1_out, i1);
  and and_1 (and_1_out, not_1_out, not_2_out);
  not not_2 (not_2_out, i3);
  not not_3 (not_3_out, i0);
  and and_2 (and_2_out, not_3_out, i2);
  not not_4 (not_4_out, i0);
  and and_3 (and_3_out, not_4_out, i1, i3);
  and and_4 (and_4_out, i1, i2);
  and and_5 (and_5_out, i0, not_5_out, not_6_out);
  not not_5 (not_5_out, i1);
  not not_6 (not_6_out, i2);
  and and_6 (and_6_out, i0, not_7_out);
  not not_7 (not_7_out, i3);
  not not_8 (not_8_out, i0);
  and and_7 (and_7_out, not_8_out, not_9_out);
  not not_9 (not_9_out, i1);
  not not_10 (not_10_out, i0);
  and and_8 (and_8_out, not_10_out, not_11_out, not_12_out);
  not not_11 (not_11_out, i2);
  not not_12 (not_12_out, i3);
  not not_13 (not_13_out, i1);
  and and_9 (and_9_out, not_13_out, not_14_out);
  not not_14 (not_14_out, i3);
  not not_15 (not_15_out, i0);
  and and_10 (and_10_out, not_15_out, i2, i3);
  and and_11 (and_11_out, i0, not_16_out, i3);
  not not_16 (not_16_out, i2);
  not not_17 (not_17_out, i0);
  and and_12 (and_12_out, not_17_out, not_18_out);
  not not_18 (not_18_out, i2);
  not not_19 (not_19_out, i0);
  and and_13 (and_13_out, not_19_out, i3);
  not not_20 (not_20_out, i2);
  and and_14 (and_14_out, not_20_out, i3);
  not not_21 (not_21_out, i0);
  and and_15 (and_15_out, not_21_out, i1);
  and and_16 (and_16_out, i0, not_22_out);
  not not_22 (not_22_out, i1);
  not not_23 (not_23_out, i0);
  and and_17 (and_17_out, not_23_out, not_24_out, not_25_out);
  not not_24 (not_24_out, i1);
  not not_25 (not_25_out, i3);
  not not_26 (not_26_out, i1);
  and and_18 (and_18_out, not_26_out, i2, i3);
  not not_27 (not_27_out, i2);
  and and_19 (and_19_out, i1, not_27_out, i3);
  and and_20 (and_20_out, i1, i2, not_28_out);
  not not_28 (not_28_out, i3);
  not not_29 (not_29_out, i2);
  and and_21 (and_21_out, i0, not_29_out, not_30_out);
  not not_30 (not_30_out, i3);
  not not_31 (not_31_out, i1);
  and and_22 (and_22_out, not_31_out, not_32_out);
  not not_32 (not_32_out, i3);
  and and_23 (and_23_out, i2, not_33_out);
  not not_33 (not_33_out, i3);
  and and_24 (and_24_out, i0, i2);
  and and_25 (and_25_out, i0, i1);
  not not_34 (not_34_out, i2);
  and and_26 (and_26_out, not_34_out, not_35_out);
  not not_35 (not_35_out, i3);
  not not_36 (not_36_out, i0);
  and and_27 (and_27_out, not_36_out, i1, not_37_out);
  not not_37 (not_37_out, i2);
  and and_28 (and_28_out, i1, not_38_out);
  not not_38 (not_38_out, i3);
  and and_29 (and_29_out, i0, not_39_out);
  not not_39 (not_39_out, i1);
  and and_30 (and_30_out, i0, i2);
  not not_40 (not_40_out, i1);
  and and_31 (and_31_out, not_40_out, i2);
  and and_32 (and_32_out, i2, not_41_out);
  not not_41 (not_41_out, i3);
  not not_42 (not_42_out, i0);
  and and_33 (and_33_out, not_42_out, i1, not_43_out);
  not not_43 (not_43_out, i2);
  and and_34 (and_34_out, i0, not_44_out);
  not not_44 (not_44_out, i1);
  and and_35 (and_35_out, i0, i3);
  or or_1 (o2, and_7_out, and_8_out, and_9_out, and_10_out, and_11_out);
  or or_2 (o3, and_12_out, and_13_out, and_14_out, and_15_out, and_16_out);
  or or_3 (o4, and_17_out, and_18_out, and_19_out, and_20_out, and_21_out);
  or or_4 (o5, and_22_out, and_23_out, and_24_out, and_25_out);
  or or_5 (o6, and_26_out, and_27_out, and_28_out, and_29_out, and_30_out);
  or or_6 (o7, and_31_out, and_32_out, and_33_out, and_34_out, and_35_out);
  or or_7 (o1, and_1_out, and_2_out, and_3_out, and_4_out, and_5_out, and_6_out);
endmodule

module up_down_counter (
  input  Up_Down,
  input  Clock,
  input  Reset,
  output O4,
  output O3,
  output O2,
  output O1
);

  wire and_1_out, and_2_out, and_3_out, and_4_out, and_5_out, and_6_out, d_ff_1_qn, d_ff_2_qn, d_ff_3_qn,
       not_1_out, or_1_out, or_2_out, or_3_out, or_4_out, xor_1_out, xor_2_out, xor_3_out, xor_4_out;

  not not_1 (not_1_out, Up_Down);
  and and_1 (and_1_out, not_1_out, d_ff_1_qn);
  and and_2 (and_2_out, and_1_out, d_ff_2_qn);
  and and_3 (and_3_out, and_2_out, d_ff_3_qn);
  and and_4 (and_4_out, Up_Down, O1);
  and and_5 (and_5_out, and_4_out, O2);
  and and_6 (and_6_out, and_5_out, O3);
  or or_1 (or_1_out, Up_Down, not_1_out);
  or or_2 (or_2_out, and_4_out, and_1_out);
  or or_3 (or_3_out, and_5_out, and_2_out);
  or or_4 (or_4_out, and_6_out, and_3_out);
  xor xor_1 (xor_1_out, O1, or_1_out);
  xor xor_2 (xor_2_out, O2, or_2_out);
  xor xor_3 (xor_3_out, O3, or_3_out);
  xor xor_4 (xor_4_out, O4, or_4_out);
  D_Flip_Flop d_ff_1 (.clk(Clock), .D(xor_1_out), .Q(O1), .Qn(d_ff_1_qn), .reset(Reset));  // open: preset, en
  D_Flip_Flop d_ff_2 (.clk(Clock), .D(xor_2_out), .Q(O2), .Qn(d_ff_2_qn), .reset(Reset));  // open: preset, en
  D_Flip_Flop d_ff_3 (.clk(Clock), .D(xor_3_out), .Q(O3), .Qn(d_ff_3_qn), .reset(Reset));  // open: preset, en
  D_Flip_Flop d_ff_4 (.clk(Clock), .D(xor_4_out), .Q(O4), .reset(Reset));  // open: Qn, preset, en

  // Notes on the sheet:
  //   D is data comming int flip-flop
  //   Q is output signal
  //   Q' outputs inverse
  //   D flip flop
  //   en0 when activated by a reset signal forces all output to be overidden to one
  //   Holds data until clock signal
endmodule

module Final_Result (
  input  Up_Down
);

  wire _4b_decoder_o1, _4b_decoder_o2, _4b_decoder_o3, _4b_decoder_o4, _4b_decoder_o5, _4b_decoder_o6,
       _4b_decoder_o7, _4b_U_D_CNTR_o1, _4b_U_D_CNTR_o2, _4b_U_D_CNTR_o3, _4b_U_D_CNTR_o4, Clock_out,
       Reset_out;

  up_down_counter _4b_U_D_CNTR (
    .Up_Down(Up_Down), .Clock(Clock_out), .Reset(Reset_out), .O4(_4b_U_D_CNTR_o4), .O3(_4b_U_D_CNTR_o3),
    .O2(_4b_U_D_CNTR_o2), .O1(_4b_U_D_CNTR_o1));
  Button Reset (.out(Reset_out));
  Clock Clock (.out(Clock_out));
  _7_Segment_Display_decoder _4b_decoder (
    .i0(_4b_U_D_CNTR_o4), .i1(_4b_U_D_CNTR_o3), .i2(_4b_U_D_CNTR_o2), .i3(_4b_U_D_CNTR_o1),
    .o1(_4b_decoder_o1), .o2(_4b_decoder_o2), .o3(_4b_decoder_o3), .o4(_4b_decoder_o4), .o5(_4b_decoder_o5),
    .o6(_4b_decoder_o6), .o7(_4b_decoder_o7));
  _7_Segment_Display u_7_segment_display_1 (
    .g(_4b_decoder_o7), .f(_4b_decoder_o6), .a(_4b_decoder_o1), .b(_4b_decoder_o2), .e(_4b_decoder_o5),
    .d(_4b_decoder_o4), .c(_4b_decoder_o3));  // open: dp
endmodule

module test (
  input  in_1,
  input  in_2,
  input  in_3,
  input  in_4,
  input  UpDown,
  input  Clock,
  input  Button,
  output out_8,
  output out_9,
  output out_10,
  output out_11
);

  wire and_1_out, and_2_out, and_3_out, and_4_out, and_5_out, and_6_out, d_ff_1_q, d_ff_1_qn, d_ff_2_q,
       d_ff_2_qn, d_ff_3_q, d_ff_3_qn, d_ff_4_q, n7_segment_display_decoder_1_o1,
       n7_segment_display_decoder_1_o2, n7_segment_display_decoder_1_o3, n7_segment_display_decoder_1_o4,
       n7_segment_display_decoder_1_o5, n7_segment_display_decoder_1_o6, n7_segment_display_decoder_1_o7,
       not_1_out, or_1_out, or_2_out, or_3_out, or_4_out, xor_1_out, xor_2_out, xor_3_out, xor_4_out;

  up_down_backup up_down_backup_1 ();  // open: UpDown, out_2, out_3, out_4, out_5
  _7_Segment_Display_decoder u_7_segment_display_decoder_1 (
    .i0(in_1), .i1(in_2), .i2(in_3), .i3(in_4), .o1(n7_segment_display_decoder_1_o1),
    .o2(n7_segment_display_decoder_1_o2), .o3(n7_segment_display_decoder_1_o3),
    .o4(n7_segment_display_decoder_1_o4), .o5(n7_segment_display_decoder_1_o5),
    .o6(n7_segment_display_decoder_1_o6), .o7(n7_segment_display_decoder_1_o7));
  _7_Segment_Display u_7_segment_display_1 (
    .g(n7_segment_display_decoder_1_o7), .f(n7_segment_display_decoder_1_o6),
    .a(n7_segment_display_decoder_1_o1), .b(n7_segment_display_decoder_1_o2),
    .e(n7_segment_display_decoder_1_o5), .d(n7_segment_display_decoder_1_o4),
    .c(n7_segment_display_decoder_1_o3));  // open: dp
  not not_1 (not_1_out, UpDown);
  and and_1 (and_1_out, not_1_out, d_ff_1_qn);
  and and_2 (and_2_out, and_1_out, d_ff_2_qn);
  and and_3 (and_3_out, and_2_out, d_ff_3_qn);
  and and_4 (and_4_out, UpDown, d_ff_1_q);
  and and_5 (and_5_out, and_4_out, d_ff_2_q);
  and and_6 (and_6_out, and_5_out, d_ff_3_q);
  or or_1 (or_1_out, UpDown, not_1_out);
  or or_2 (or_2_out, and_4_out, and_1_out);
  or or_3 (or_3_out, and_5_out, and_2_out);
  or or_4 (or_4_out, and_6_out, and_3_out);
  xor xor_1 (xor_1_out, d_ff_1_q, or_1_out);
  xor xor_2 (xor_2_out, d_ff_2_q, or_2_out);
  xor xor_3 (xor_3_out, d_ff_3_q, or_3_out);
  xor xor_4 (xor_4_out, d_ff_4_q, or_4_out);
  D_Flip_Flop d_ff_1 (.clk(Clock), .D(xor_1_out), .Q(d_ff_1_q), .Qn(d_ff_1_qn), .reset(Button));  // open: preset, en
  D_Flip_Flop d_ff_2 (.clk(Clock), .D(xor_2_out), .Q(d_ff_2_q), .Qn(d_ff_2_qn), .reset(Button));  // open: preset, en
  D_Flip_Flop d_ff_3 (.clk(Clock), .D(xor_3_out), .Q(d_ff_3_q), .Qn(d_ff_3_qn), .reset(Button));  // open: preset, en
  D_Flip_Flop d_ff_4 (.clk(Clock), .D(xor_4_out), .Q(d_ff_4_q), .reset(Button));  // open: Qn, preset, en
  not not_2 (out_8, d_ff_1_q);
  not not_3 (out_9, d_ff_2_q);
  not not_4 (out_10, d_ff_3_q);
  not not_5 (out_11, d_ff_4_q);
endmodule

// test
module up_down_backup (
  input  UpDown,
  output out_2,
  output out_3,
  output out_4,
  output out_5
);

  wire and_1_out, and_2_out, and_3_out, and_4_out, and_5_out, and_6_out, Clock_out, d_ff_1_q, d_ff_1_qn,
       d_ff_2_q, d_ff_2_qn, d_ff_3_q, d_ff_3_qn, d_ff_4_q, not_1_out, or_1_out, or_2_out, or_3_out, or_4_out,
       Reset_out, xor_1_out, xor_2_out, xor_3_out, xor_4_out;

  not not_1 (not_1_out, UpDown);
  and and_1 (and_1_out, not_1_out, d_ff_1_qn);
  and and_2 (and_2_out, and_1_out, d_ff_2_qn);
  and and_3 (and_3_out, and_2_out, d_ff_3_qn);
  and and_4 (and_4_out, UpDown, d_ff_1_q);
  and and_5 (and_5_out, and_4_out, d_ff_2_q);
  and and_6 (and_6_out, and_5_out, d_ff_3_q);
  or or_1 (or_1_out, UpDown, not_1_out);
  or or_2 (or_2_out, and_4_out, and_1_out);
  or or_3 (or_3_out, and_5_out, and_2_out);
  or or_4 (or_4_out, and_6_out, and_3_out);
  xor xor_1 (xor_1_out, d_ff_1_q, or_1_out);
  xor xor_2 (xor_2_out, d_ff_2_q, or_2_out);
  xor xor_3 (xor_3_out, d_ff_3_q, or_3_out);
  xor xor_4 (xor_4_out, d_ff_4_q, or_4_out);
  D_Flip_Flop d_ff_1 (
    .clk(Clock_out), .D(xor_1_out), .Q(d_ff_1_q), .Qn(d_ff_1_qn), .reset(Reset_out));  // open: preset, en
  D_Flip_Flop d_ff_2 (
    .clk(Clock_out), .D(xor_2_out), .Q(d_ff_2_q), .Qn(d_ff_2_qn), .reset(Reset_out));  // open: preset, en
  D_Flip_Flop d_ff_3 (
    .clk(Clock_out), .D(xor_3_out), .Q(d_ff_3_q), .Qn(d_ff_3_qn), .reset(Reset_out));  // open: preset, en
  D_Flip_Flop d_ff_4 (.clk(Clock_out), .D(xor_4_out), .Q(d_ff_4_q), .reset(Reset_out));  // open: Qn, preset, en
  Clock Clock (.out(Clock_out));
  Button Reset (.out(Reset_out));
  not not_2 (out_2, d_ff_1_q);
  not not_3 (out_3, d_ff_2_q);
  not not_4 (out_4, d_ff_3_q);
  not not_5 (out_5, d_ff_4_q);
endmodule

module adder (
  input  a,
  input  b,
  input  ci,
  output Sum,
  output Cout
);

  wire and_1_out, and_2_out, xor_1_out;

  xor xor_1 (xor_1_out, a, b);
  and and_1 (and_1_out, a, b);
  xor xor_2 (Sum, xor_1_out, ci);
  and and_2 (and_2_out, xor_1_out, ci);
  or or_1 (Cout, and_1_out, and_2_out);

  // Notes on the sheet:
  //   Cout = ab + ci(a xor b)
  //   Sum = a xor b xor c xor ci
  //   ab
  //   a XOR b
  //   a XOR b XOR Ci
  //   Ci(a XOR b)
endmodule

module _4_bit_adder (
  input  a0,
  input  a1,
  input  a2,
  input  a3,
  input  b0,
  input  b1,
  input  b2,
  input  b3,
  input  Ci,
  output Co,
  output s3,
  output s2,
  output s1,
  output s0
);

  wire adder_1_cout, adder_2_cout, adder_3_cout;

  adder adder_1 (.a(a0), .b(b0), .ci(Ci), .Sum(s0), .Cout(adder_1_cout));
  adder adder_2 (.a(a1), .b(b1), .ci(adder_1_cout), .Sum(s1), .Cout(adder_2_cout));
  adder adder_3 (.a(a2), .b(b2), .ci(adder_2_cout), .Sum(s2), .Cout(adder_3_cout));
  adder adder_4 (.a(a3), .b(b3), .ci(adder_3_cout), .Sum(s3), .Cout(Co));
endmodule

module up_down_counter_W_adder (
  input  Reset
);

  D_Flip_Flop d_ff_1 (.reset(Reset));  // open: clk, D, Q, Qn, preset, en
  D_Flip_Flop d_ff_2 (.reset(Reset));  // open: clk, D, Q, Qn, preset, en
  D_Flip_Flop d_ff_3 (.reset(Reset));  // open: clk, D, Q, Qn, preset, en
  D_Flip_Flop d_ff_4 (.reset(Reset));  // open: clk, D, Q, Qn, preset, en
  _4_bit_adder u_4_bit_adder_1 ();  // open: Ci, a0, a1, a2, a3, b0, b1, b2, b3, s3, s2, s1, s0, Co
endmodule
